# Fritzing sketch buttons-red (saved by Fritzing 0.9.5d)
circuit board: 9.94879cm x 2.09533cm
breadboards: 1

parts:
  Onderdeel7 = LED Tactile Button 12mm [part_number=BOB-10467]
  Onderdeel8 = LED Tactile Button 12mm [part_number=BOB-10467]
  Onderdeel9 = LED Tactile Button 12mm [part_number=BOB-10467]
  Onderdeel10 = LED Tactile Button 12mm [part_number=BOB-10467]
  Onderdeel11 = LED Tactile Button 12mm [part_number=BOB-10467]
  R1 = Resistor [tolerance=±5% resistance=2.2k package=THT]
  R2 = Resistor [tolerance=±5% resistance=2.2k package=THT]
  R3 = Resistor [tolerance=±5% resistance=2.2k package=THT]
  R4 = Resistor [tolerance=±5% resistance=2.2k package=THT]
  R5 = Resistor [tolerance=±5% resistance=220 package=THT]
  J1 = female pin header, 9 pins [form="♀ (female)"]  # not connected

nets:
  N1: Onderdeel7.pin_2, Onderdeel8.pin_2, Onderdeel10.pin_2, Onderdeel11.pin_2
  N2: Onderdeel7.pin_3, Onderdeel7.pin_5, R1.Pin_0, R5.Pin_1
  N3: Onderdeel7.pin_4, Onderdeel7.pin_6, Onderdeel8.pin_4, Onderdeel8.pin_6, Onderdeel9.pin_4, Onderdeel9.pin_6, Onderdeel10.pin_4, Onderdeel10.pin_6, Onderdeel11.pin_6
  N4: Onderdeel8.pin_3, Onderdeel8.pin_5, R1.Pin_1, R2.Pin_0
  N5: Onderdeel9.pin_3, Onderdeel9.pin_5, R2.Pin_1, R3.Pin_0
  N6: Onderdeel10.pin_3, Onderdeel10.pin_5, R3.Pin_1, R4.Pin_0
  N7: Onderdeel11.pin_5, R4.Pin_1

notes:
  digit
  analog in
  GND
  vdd
  segA
  segB
  segC
  segD
  segE

custom parts:
  LED Tactile Button 12mm: A LED tactile switch
